# Fritzing sketch datalogger (saved by Fritzing 0.9.3b)
breadboards: 1

parts:
  C1 = Tantalum Capacitor [capacitance=100nF package="B 3528 [SMD, tantalum]"]
  C3 = Tantalum Capacitor [capacitance=100nF package="B 3528 [SMD, tantalum]"]
  C2 = Tantalum Capacitor [capacitance=0.1nF package="B 3528 [SMD, tantalum]"]
  Power_plug1 = Power plug
  U1 = Voltage Regulator [package=v-reg_dpack]
  U2 = SD_CARD_SOCKET [package=sdcard_4uconn]
  U3 = ATmega328 [package=tqfp]
  RESET = Pushbutton [package="[THT]"]
  R1 = Resistor [tolerance=±5% resistance=1M package="1206 [SMD]"]
  L1 = Inductor [inductance=10nH package="1206 [SMD]"]
  C4 = Ceramic Capacitor [capacitance=100nF package="1206 [SMD, multilayer]"]
  Q1 = Basic FET P-Channel [package="DPak [SMD]"]
  J1 = male pin header, 6 pins [form="♂ (male)"]
  C5 = Ceramic Capacitor [capacitance=100nF package="1206 [SMD, multilayer]"]
  IC1 = SO16w [chip_label=DS3231SN package=SO(w)]
  BAT1 = Battery Holders [package=battcon_20mm]
  WAKE_UP = Pushbutton [package="[THT]"]
  R2 = Resistor [tolerance=±5% resistance=10k package="1206 [SMD]"]
  R3 = Resistor [tolerance=±5% resistance=10k package="1206 [SMD]"]
  C6 = Electrolytic Capacitor [capacitance=1µF package="0405 [SMD, electrolytic]"]

nets:
  GND: C1.-, C3.-, C2.-, Power_plug1.GND, U1.ADJ, U2.SH, U2.VSS1, U2.VSS2, U3.GND, RESET.Pin_4, C4.0, J1.pin1, J1.pin2, IC1.5, IC1.6, IC1.7, IC1.8, IC1.9, IC1.10, IC1.11, IC1.12, IC1.13, BAT1.-, WAKE_UP.Pin_2, C6.-
  6V: C1.+, Power_plug1.VCC, U1.IN, J1.pin3
  3.3V: C3.+, C2.+, U1.OUT, U2.VDD, U3.VCC, U3.AREF, R1.Pin_0, L1.pin_0, Q1.source, IC1.2, R2.Pin_0, R3.Pin_0
  CS: U2.CD_DAT3, U3.PB2(SS_OC1B)
  MOSI: U2.CMD, U3.PB3(MOSI_OC2)
  SCK: U2.CLK, U3.PB5(SCK)
  MISO: U2.DAT0, U3.PB4(MISO)
  N1: U3.PD5(T1), Q1.Gate
  AVCC: U3.AVCC, L1.pin_1, C4.1
  INT/SQW: U3.PC2(ADC2), IC1.3, WAKE_UP.Pin_3, WAKE_UP.Pin_4
  SDA: U3.PC4(ADC4_SDA), IC1.15, R3.Pin_1
  SCL: U3.PC5(ADC5_SCL), IC1.16, R2.Pin_1
  RESET: U3.PC6(_RESET), RESET.Pin_2, R1.Pin_1, C5.1
  N2: U3.PD0(RXD), J1.pin4
  N3: U3.PD1(TXD), J1.pin5
  VSS Switched: Q1.drain
  N4: J1.pin6, C5.0
  32kHz: IC1.1
  N5: IC1.14, BAT1.+, C6.+

notes:
  UW Datalogger, A datalogger for long term deployment. , 2
